# Fritzing sketch vertical-blind (saved by Fritzing 0.9.3b)

parts:
  U1 = ESP32-38PinWide [part_number=ESP32-38PinWide]
  R1 = Photocell (LDR) [package=THT]
  R2 = Photocell (LDR) [package=THT]
  R3 = Photocell (LDR) [package=THT]
  R4 = Photocell (LDR) [package=THT]
  SM1 = 28BYJ-48 Stepper Motor [part_number=28BYJ-48]
  Driver1 = 28BYJ-48 Driver Module [part_number=ULN2003 package=THT]
  SM2 = 28BYJ-48 Stepper Motor [part_number=28BYJ-48]
  Driver2 = 28BYJ-48 Driver Module [part_number=ULN2003 package=THT]
  J1 = Screw terminal - 2 pins [package=THT]
  A1 = Adafruit ADS1115 ADC
  R5 = Resistor [tolerance=±5% resistance=10k package=THT]
  R6 = Resistor [tolerance=±5% resistance=10k package=THT]
  R7 = Resistor [tolerance=±5% resistance=10k package=THT]
  R8 = Resistor [tolerance=±5% resistance=10k package=THT]

nets:
  VIN: U1.3.3, R1.pin_0, R2.pin_0, R3.pin_0, R4.pin_0, A1.VIN, A1.VCC
  GND: U1.GND, A1.GND, A1.ADDR, R5.Pin_0, R6.Pin_0, R7.Pin_0, R8.Pin_0
  N1: U1.GPIO15, Driver1.IN4
  N2: U1.GPIO2, Driver1.IN3
  N3: U1.GPIO4, Driver1.IN2
  N4: U1.GPIO16, Driver1.IN1
  N5: U1.GPIO17, Driver2.IN4
  N6: U1.GPIO5, Driver2.IN3
  N7: U1.GPIO18, Driver2.IN2
  N8: U1.GPIO19, Driver2.IN1
  N9: U1.GPIO1, A1.SDA
  N10: U1.GPIO22, A1.SCL
  N11: R1.pin_1, A1.A3, R5.Pin_1
  N12: R2.pin_1, A1.A2, R6.Pin_1
  N13: R3.pin_1, A1.A0, R8.Pin_1
  N14: R4.pin_1, A1.A1, R7.Pin_1
  N15: SM1.blue-pin, Driver1.blue-pin
  N16: SM1.pink-pin, Driver1.pink-pin
  N17: SM1.yellow-pin, Driver1.yellow-pin
  N18: SM1.orange-pin, Driver1.orange-pin
  N19: SM1.red-pin, Driver1.red-pin
  GND_2: Driver1.GND, Driver2.GND, J1.pin2
  N20: Driver1.Vmotor, Driver2.Vmotor, J1.pin1
  N21: SM2.blue-pin, Driver2.blue-pin
  N22: SM2.pink-pin, Driver2.pink-pin
  N23: SM2.yellow-pin, Driver2.yellow-pin
  N24: SM2.orange-pin, Driver2.orange-pin
  N25: SM2.red-pin, Driver2.red-pin

custom parts:
  ESP32-38PinWide: Generic 38-Pin ESP32 with wide format (only access to one side of pins on a breadboard) based on Stephen Lilley's HiLetgo ESP-WROOM-32 ESP32 ESP-32S Development Board.
  28BYJ-48 Stepper Motor: Unipolar Stepper Motor 28BYJ-48 Top coil - pink & orange Bottom coil - blue & yellow Common rail - red Connector pins: blue - pink - yellow - orange - red
  28BYJ-48 Driver Module: High-power ULN2003 Stepper Motor Driver Board Test Module For Arduino AVR SMD
